# Fritzing sketch SmartCar (saved by Fritzing 0.9.3b)
circuit board: 10cm x 6cm

parts:
  Bluetooth_module = Bluetooth HC-05 Macho
  Left = SRF05 Ultrasonic Rangefinder
  Mid-Left = SRF05 Ultrasonic Rangefinder
  Right = SRF05 Ultrasonic Rangefinder
  Rear = SRF05 Ultrasonic Rangefinder
  Mid-Right = SRF05 Ultrasonic Rangefinder
  Mid = SRF05 Ultrasonic Rangefinder
  Voltage_sensor = Voltage Sensor Module
  Battery_pack = 4 x AAA Battery Mount
  Arduino_Mega = Arduino Mega 2560 (Rev3)
  Compass = Adafruit LSM303DLHC Triple-axis Accelerometer+Magnetometer (Compass) [part_number="Adafruit #1120"]

nets:
  N1: Bluetooth_module.TXD, Arduino_Mega.D15/RX3
  N2: Bluetooth_module.RXD, Arduino_Mega.D14/TX3
  N3: Left.Trig, Arduino_Mega.D35
  N4: Left.Echo, Arduino_Mega.D34
  N5: Mid-Left.Trig, Arduino_Mega.D43
  N6: Mid-Left.Echo, Arduino_Mega.D42
  N7: Right.Trig, Arduino_Mega.D33
  N8: Right.Echo, Arduino_Mega.D32
  N9: Rear.Trig, Arduino_Mega.D23
  N10: Rear.Echo, Arduino_Mega.D22
  N11: Mid-Right.Trig, Arduino_Mega.D51
  N12: Mid-Right.Echo, Arduino_Mega.D50
  N13: Mid.Trig, Arduino_Mega.D49
  N14: Mid.Echo, Arduino_Mega.D48
  N15: Voltage_sensor.OUT, Arduino_Mega.A0
  N16: Voltage_sensor.INPUT+, Battery_pack.+
  N17: Voltage_sensor.INPUT-, Battery_pack.-
  N18: Arduino_Mega.D21/SCL, Arduino_Mega.SCL, Compass.SCL
  N19: Arduino_Mega.D20/SDA, Arduino_Mega.SDA, Compass.SDA
  5V: Arduino_Mega.5V, Compass.VIN
  GND: Arduino_Mega.GND, Compass.GND

notes:
  Ultrasonic sensor
  Sensor Arduino (Trigger/Echo)
  Right 33/32 (digital)
  Mid-Right 51/50 (digital)
  Mid 49/48 (digital)
  Mid-Left 43/42 (digital)
  Left 35/34 (digital)
  Rear 23/22 (digital)
  GND GND
  VCC 5 V
  Bluetooth module
  Module Arduino(communication)
  TXD RX3/15
  RXD TX3/14
  GND GND
  VCC 5 V
  Voltage sensor
  Sensor Arduino
  S A0 (analog in)
  - GND
  Sensor Batterypack
  GND Negative terminal
  VCC Positive terminal
  Adafruit compass
  Compass Arduino
  GND GND
  VIN 5V
  SDA SDA (A4 on classic Arduinos)
  SCL SCL (A5 on classic Arduinos)
  Adafruit compass
  Compass Arduino
  GND GND
  VIN 5V
  SDA SDA (A4)
  SCL SCL (A5)

custom parts:
  Adafruit LSM303DLHC Triple-axis Accelerometer+Magnetometer (Compass): He told you "Go West, young maker!" - but you don't know which way is West! Ah, if only you had this triple-axis accelerometer/magnetometer compass module. Inside are two sensors, one is a classic 3-axis accelerometer, which can tell you which direction is down towards the Earth (by measuring gravity). The other is a magnetometer that can sense where the strongest magnetic force is coming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
